# Fritzing sketch board (saved by Fritzing 0.9.3b)
breadboards: 2

parts:
  Q2 = npn-Powertransistor [package="TO220 [THT]"]
  Part1 = Arduino Uno (Rev3)
  R1 = Resistor [tolerance=±5% resistance=220 package=THT]
  D1 = Rectifier Diode [part_number=1N4001 package="300 mil [THT]"]
  Part3 = Arduino Nano (Rev3.0)
  Part4 = RFID-RC522-v2
  M1 = DC Motor

nets:
  N1: Q2.base, R1.Pin_1
  N2: Q2.collector, D1.cathode, M1.pin_1
  GND: Q2.emitter, Part1.GND, D1.anode, Part3.GND, Part4.GND
  N3: Part1.A4/SDA, Part3.A4
  N4: Part1.A5/SCL, Part3.A5
  N5: Part1.D9_PWM, R1.Pin_0
  5V: Part1.5V, Part3.VIN, M1.pin_2
  N6: Part3.D9, Part4.RST
  N7: Part3.D10, Part4.SDA
  N8: Part3.D11/MOSI, Part4.MOSI
  N9: Part3.D12/MISO, Part4.MISO
  3V3: Part3.3V3, Part4.3.3V
  N10: Part3.D13/SCK, Part4.SCK

custom parts:
  RFID-RC522-v2: A simple China made RFID-RC522 Reader; do check the pin labels, as this is a MFRC522 based clone.
